# Fritzing sketch ohm meter using arduino (saved by Fritzing 0.9.3b)
breadboards: 1

parts:
  R1_known_resistance = Resistor [tolerance=±5% resistance=680 package=THT]
  R2_unknown_resistance = Resistor [tolerance=±5% resistance=220 package=THT]
  Composant1 = Arduino Uno (Rev3)

nets:
  N1: R1_known_resistance.Pin_0, Composant1.GND
  N2: R1_known_resistance.Pin_1, R2_unknown_resistance.Pin_0, Composant1.A0
  N3: R2_unknown_resistance.Pin_1, Composant1.5V
